# Fritzing sketch Schema (saved by Fritzing 0.9.3b)
breadboards: 1

parts:
  Componente1 = SparkFun ESP8266 Thing
  Part1 = Altitude/Pressure Sensor - MPL3115A2 Breakout [part_number=SEN-11084]

nets:
  GND: Componente1.GND, Part1.GND
  VCC: Componente1.VCC, Part1.VCC
  N1: Componente1.GPIO2, Part1.SDA
  N2: Componente1.GPIO14, Part1.SCL
